// Logisim project lc3_simulator.circ as structural Verilog: 1 circuit, main circuit main
module main (
  input  in_1,
  input  [15:0] Reset_Values,
  input  [2:0] Interrupts,
  input  [2:0] in_4,
  input  [7:0] in_5,
  input  [15:0] in_6,
  output [5:0] _2,
  output out_8,
  output [15:0] out_9,
  output [5:0] _16,
  output [2:0] out_11,
  output [15:0] out_12,
  output [48:0] out_13,
  output [2:0] out_14,
  output [15:0] out_15,
  output [15:0] out_16,
  output out_17,
  output out_18,
  output out_19,
  output [1:0] out_20,
  output out_21,
  output [2:0] out_22,
  output out_23,
  output out_24,
  output [1:0] out_25,
  output out_26,
  output [5:0] out_27,
  output out_28,
  output out_29,
  output [1:0] out_30,
  output out_31,
  output out_32,
  output out_33,
  output out_34,
  output out_35,
  output out_36,
  output out_37,
  output [1:0] out_38,
  output out_39,
  output out_40,
  output out_41,
  output [1:0] out_42,
  output out_43,
  output out_44,
  output out_45,
  output out_46,
  output out_47,
  output out_48,
  output out_49,
  output [1:0] out_50,
  output out_51,
  output out_52,
  output [2:0] out_53,
  output out_54,
  output [1:0] out_55,
  output [2:0] out_56,
  output out_57
);

  wire and_1_out, and_2_out, and_4_out, and_5_out, and_6_out, and_7_out, and_10_out, and_12_out, and_13_out,
       and_14_out, and_16_out, and_18_out, and_19_out, and_20_out, and_22_out, and_23_out, and_24_out,
       and_25_out, and_26_out, clock_1_out, clock_2_out, clock_3_out, clock_4_out, clock_5_out, clock_7_out,
       clock_8_out, clock_9_out, clock_10_out, clock_11_out, clock_12_out, clock_13_out, clock_14_out,
       clock_15_out, clock_16_out, clock_17_out, clock_18_out, clock_19_out, decoder_4_out0, decoder_4_out1,
       decoder_4_out2, DEnable, KBEnable, KBRdy, KeyR, LD_DDR, LD_DSR, LD_KBSR, MEM_EN, multiplexer_6_out,
       not_1_out, not_2_out, not_3_out, not_4_out, not_5_out, not_7_out, not_9_out, or_3_out, or_4_out,
       or_5_out, or_6_out, or_7_out, or_9_out, or_10_out, SET_KBSR, xDevReg;
  wire [1:0] and_9_out, and_15_out, INMUX;
  wire [2:0] decoder_3_out5, multiplexer_7_out, multiplexer_8_out, multiplexer_12_out;
  wire [4:0] decoder_3_out0, or_15_out;
  wire [5:0] multiplexer_21_out, register_1_q;
  wire [6:0] DChar, KBChar;
  wire [7:0] decoder_2_out0, decoder_5_out0, multiplexer_18_out, Vector_q;
  wire [14:0] KBSR_q;
  wire [15:0] adder_1_out, adder_2_out, adder_4_out, adder_5_out, adder_6_out, and_21_out,
       bit_extender_1_out, bit_extender_2_out, bit_extender_3_out, bit_extender_4_out, bit_extender_5_out,
       controlled_buffer_6_out, controlled_buffer_14_out, controlled_buffer_22_out, DSR_q, KBDR_q, MAR_q,
       MDR_q, Memory_dout, multiplexer_1_out, multiplexer_2_out, multiplexer_3_out, multiplexer_4_out,
       multiplexer_5_out, multiplexer_9_out, multiplexer_10_out, multiplexer_11_out, multiplexer_13_out,
       multiplexer_14_out, multiplexer_16_out, multiplexer_17_out, multiplexer_20_out, not_8_out, R0_q, R1_q,
       R2_q, R3_q, R4_q, R5_q, R6_q, R7_q, SSP_q, USP_q;
  wire [15:7] DDR_q;
  wire [48:0] controlled_buffer_28_out;
  wire [63:0] ControlStore_data;

  Clock clock_1 (.out(clock_1_out));
  Clock clock_2 (.out(clock_2_out));
  and and_1 (and_1_out, MAR_q[11], MAR_q[10], MAR_q[9]);
  and and_2 (and_2_out, MAR_q[15], MAR_q[14], MAR_q[13], MAR_q[12]);
  and and_3 (xDevReg, and_2_out, and_1_out);
  not not_1 (not_1_out, clock_1_out);
  TTY #(.rows(12)) tty_1 (.data(DChar), .clk(not_1_out), .we(DEnable), .clr(in_1));
  not not_2 (not_2_out, clock_2_out);
  Keyboard keyboard_1 (.clk(not_2_out), .re(KBEnable), .clr(in_1), .avail(KBRdy), .data(KBChar));
  and and_4 (and_4_out, ~MAR_q[8], ~MAR_q[7], ~MAR_q[6], ~MAR_q[5]);  // AND_Gate
  and and_5 (and_5_out, and_4_out, and_6_out);
  not not_3 (not_3_out, xDevReg);
  Clock clock_3 (.out(clock_3_out));
  Register #(.width(16)) MAR (.D(out_16), .en(out_13[38]), .clk(clock_4_out), .Q(MAR_q), .clr(in_1));
  Clock clock_4 (.out(clock_4_out));
  and and_6 (and_6_out, ~MAR_q[4], ~MAR_q[3], ~MAR_q[0]);  // AND_Gate
  and and_7 (and_7_out, and_5_out, xDevReg);
  and and_8 (and_9_out[1], and_7_out, MAR_q[2]);
  or or_1 (INMUX[1], not_3_out, and_9_out[1]);
  or or_2 (INMUX[0], not_3_out, and_9_out[0]);
  assign bit_extender_1_out = {{8{1'b0}}, out_15[7:0]};  // Bit_Extender bit_extender_1
  assign bit_extender_2_out = {{5{out_15[10]}}, out_15[10:0]};  // Bit_Extender bit_extender_2
  assign bit_extender_3_out = {{7{out_15[8]}}, out_15[8:0]};  // Bit_Extender bit_extender_3
  assign bit_extender_4_out = {{10{out_15[5]}}, out_15[5:0]};  // Bit_Extender bit_extender_4
  Register #(.width(16)) IR (.D(out_16), .en(out_13[36]), .clk(clock_3_out), .Q(out_15));  // open: clr
  and and_9 (and_9_out[0], MAR_q[1], and_7_out);
  and and_10 (and_10_out, and_7_out, out_13[2], out_13[1]);
  Decoder #(.select(2)) decoder_1 (
    .out0(LD_KBSR), .out2(LD_DSR), .out3(LD_DDR), .sel(and_9_out), .en(and_10_out));  // open: out1
  assign out_16 = out_13[24] ? multiplexer_1_out : 16'bz;  // Controlled_Buffer controlled_buffer_1
  Multiplexer #(.width(16)) multiplexer_1 (
    .in0(bit_extender_1_out), .in1(adder_1_out), .out(multiplexer_1_out), .sel(out_13[8]));
  // Probe on out_16
  and and_11 (MEM_EN, out_13[2], ~xDevReg);  // AND_Gate
  and and_12 (and_12_out, out_13[2], ~out_43);  // AND_Gate
  D_Flip_Flop #(.trigger("falling")) IoR (.D(and_12_out), .clk(clock_5_out), .Q(out_43));  // open: Qn, preset, reset
  Clock clock_5 (.out(clock_5_out));
  Clock clock_6 ();  // open: out
  Multiplexer #(.select(2), .width(16)) multiplexer_2 (
    .in0({16{1'b0}}), .in1(bit_extender_4_out), .in2(bit_extender_3_out), .in3(bit_extender_2_out),
    .out(multiplexer_2_out));  // open: sel
  Clock clock_7 (.out(clock_7_out));
  and and_13 (and_13_out, out_13[1], MEM_EN);
  and and_14 (and_14_out, MEM_EN, ~out_13[1]);  // AND_Gate
  Adder #(.width(16)) adder_1 (.a(multiplexer_2_out), .b(multiplexer_5_out), .out(adder_1_out));  // open: cin, cout
  RAM #(.addrWidth(16), .dataWidth(16)) Memory (
    .addr(MAR_q), .we(and_13_out), .oe(and_14_out), .clk(clock_7_out), .din(MDR_q), .dout(Memory_dout));
  not not_4 (not_4_out, DEnable);
  not not_5 (not_5_out, in_1);
  Register #(.width(16)) PC (.D(multiplexer_3_out), .en(or_3_out), .clk(clock_8_out), .Q(out_12));  // open: clr
  Multiplexer #(.width(16)) multiplexer_3 (
    .in0(Reset_Values), .in1(multiplexer_4_out), .out(multiplexer_3_out), .sel(not_5_out));
  or or_3 (or_3_out, in_1, out_13[32]);
  Clock clock_8 (.out(clock_8_out));
  Multiplexer #(.select(2), .width(16)) multiplexer_4 (
    .in0(adder_2_out), .in1(out_16), .in2(adder_1_out), .out(multiplexer_4_out), .sel(out_13[19:18]));  // open: in3
  Multiplexer #(.width(16)) multiplexer_5 (
    .in0(out_12), .in1(controlled_buffer_14_out), .out(multiplexer_5_out), .sel(out_13[13]));
  Multiplexer multiplexer_6 (.in0(out_13[0]), .in1(out_16[15]), .out(multiplexer_6_out), .sel(out_13[5]));
  Multiplexer #(.width(3)) multiplexer_7 (
    .in0(Interrupts), .in1(out_16[10:8]), .out(multiplexer_7_out), .sel(out_13[5]));
  and and_15 (and_15_out[0], ~out_16[15], ~and_15_out[1]);  // AND_Gate
  Comparator #(.width(16)) comparator_1 (.a(out_16), .b({16{1'b0}}), .eq(and_15_out[1]));  // open: gt, lt
  or or_4 (or_4_out, LD_KBSR, SET_KBSR);
  Clock clock_9 (.out(clock_9_out));
  or or_5 (or_5_out, LD_DSR, not_4_out);
  or or_6 (or_6_out, LD_DDR, DEnable);
  assign out_16 = out_13[27] ? out_12 : 16'bz;  // Controlled_Buffer controlled_buffer_2
  Adder #(.width(16)) adder_2 (.a(16'h1), .b(out_12), .out(adder_2_out));  // open: cin, cout
  Clock clock_10 (.out(clock_10_out));
  Clock clock_11 (.out(clock_11_out));
  Multiplexer #(.width(3)) multiplexer_8 (
    .in0({out_16[15], and_15_out}), .in1(out_16[2:0]), .out(multiplexer_8_out), .sel(out_13[5]));
  Register #(.trigger("falling"), .width(16)) KBSR (
    .D(multiplexer_9_out), .en(or_4_out), .clk(clock_9_out), .Q({KeyR, KBSR_q}), .clr(in_1));
  Multiplexer #(.width(16)) multiplexer_9 (
    .in0(MDR_q), .in1({KBRdy, {15{1'b0}}}), .out(multiplexer_9_out), .sel(SET_KBSR));
  Register #(.trigger("falling"), .width(16)) KBDR (
    .D({{9{1'b0}}, KBChar}), .en(SET_KBSR), .clk(clock_9_out), .Q(KBDR_q), .clr(in_1));
  Register #(.trigger("falling"), .width(16)) DSR (
    .D(multiplexer_10_out), .en(or_5_out), .clk(clock_12_out), .Q(DSR_q));  // open: clr
  Multiplexer #(.width(16)) multiplexer_10 (.in0(MDR_q), .in1(16'h8000), .out(multiplexer_10_out), .sel(not_4_out));
  Register #(.trigger("falling"), .width(16)) DDR (
    .D(multiplexer_11_out), .en(or_6_out), .clk(clock_12_out), .Q({DDR_q, DChar}));  // open: clr
  Multiplexer #(.width(16)) multiplexer_11 (.in0(MDR_q), .in1({16{1'b0}}), .out(multiplexer_11_out), .sel(DEnable));
  Clock clock_12 (.out(clock_12_out));
  D_Flip_Flop Priv (.D(multiplexer_6_out), .clk(and_16_out), .Q(out_8), .preset(in_1));  // open: Qn, reset
  and and_16 (and_16_out, out_13[31], clock_10_out);
  Register #(.width(3)) Priority (.D(multiplexer_7_out), .en(out_13[31]), .clk(clock_11_out), .Q(out_11), .clr(in_1));
  Register #(.width(3)) CC (.D(multiplexer_12_out), .en(or_7_out), .clk(clock_13_out), .Q(out_14));  // open: clr
  Multiplexer #(.width(3)) multiplexer_12 (.in0(multiplexer_8_out), .in1(in_4), .out(multiplexer_12_out), .sel(in_1));
  or or_7 (or_7_out, out_13[33], in_1);
  Clock clock_13 (.out(clock_13_out));
  Multiplexer #(.select(2), .width(16)) multiplexer_13 (
    .in0({KeyR, KBSR_q}), .in1(KBDR_q), .in2(DSR_q), .in3(Memory_dout), .out(multiplexer_13_out), .sel(INMUX));
  assign out_16 = out_13[22] ? out_9 : 16'bz;  // Controlled_Buffer controlled_buffer_3
  Comparator #(.width(3)) comparator_2 (.a(out_11), .b(Interrupts), .lt(out_39));  // open: gt, eq
  Multiplexer #(.width(16)) multiplexer_14 (
    .in0(out_16), .in1(multiplexer_13_out), .out(multiplexer_14_out), .sel(out_13[2]));
  not not_6 (KBEnable, KeyR);
  and and_17 (SET_KBSR, ~KeyR, KBRdy);  // AND_Gate
  or or_8 (DEnable, DChar[0], DChar[1], DChar[2], DChar[3], DChar[4], DChar[5], DChar[6]);
  Decoder #(.select(3)) decoder_2 (
    .out0(decoder_2_out0[0]), .out1(decoder_2_out0[1]), .out2(decoder_2_out0[2]), .out3(decoder_2_out0[3]),
    .out4(decoder_2_out0[4]), .out5(decoder_2_out0[5]), .out6(decoder_2_out0[6]), .out7(decoder_2_out0[7]),
    .sel(out_53), .en(out_13[34]));
  Multiplexer #(.select(2), .width(3)) multiplexer_15 (
    .in0(out_15[11:9]), .in1(3'b111), .in2(3'b110), .out(out_53));  // open: in3, sel
  Adder #(.width(16)) adder_3 (.a({16{1'b1}}), .b(out_12), .out(out_9));  // open: cin, cout
  assign out_16 = out_13[21] ? {out_8, 4'b0000, out_11, {5{1'b0}}, out_14} : 16'bz;  // Controlled_Buffer controlled_buffer_4
  Register #(.width(16)) MDR (.D(multiplexer_14_out), .en(out_13[37]), .clk(clock_14_out), .Q(MDR_q), .clr(in_1));
  Clock clock_14 (.out(clock_14_out));
  assign out_16 = out_13[26] ? MDR_q : 16'bz;  // Controlled_Buffer controlled_buffer_5
  Register #(.width(16)) R0 (.D(out_16), .en(decoder_2_out0[0]), .clk(clock_15_out), .Q(R0_q));  // open: clr
  Clock clock_15 (.out(clock_15_out));
  Register #(.width(16)) R1 (.D(out_16), .en(decoder_2_out0[1]), .clk(clock_15_out), .Q(R1_q));  // open: clr
  Register #(.width(16)) R2 (.D(out_16), .en(decoder_2_out0[2]), .clk(clock_15_out), .Q(R2_q));  // open: clr
  Register #(.width(16)) R3 (.D(out_16), .en(decoder_2_out0[3]), .clk(clock_15_out), .Q(R3_q));  // open: clr
  Register #(.width(16)) R4 (.D(out_16), .en(decoder_2_out0[4]), .clk(clock_15_out), .Q(R4_q));  // open: clr
  Register #(.width(16)) R5 (.D(out_16), .en(decoder_2_out0[5]), .clk(clock_15_out), .Q(R5_q));  // open: clr
  Register #(.width(16)) R6 (.D(out_16), .en(decoder_2_out0[6]), .clk(clock_15_out), .Q(R6_q));  // open: clr
  Register #(.width(16)) R7 (.D(out_16), .en(decoder_2_out0[7]), .clk(clock_15_out), .Q(R7_q));  // open: clr
  and and_18 (and_18_out, out_15[9], out_14[0]);
  and and_19 (and_19_out, out_15[10], out_14[1]);
  and and_20 (and_20_out, out_15[11], out_14[2]);
  Decoder #(.enable("false"), .select(3)) decoder_3 (
    .out0(decoder_3_out0[0]), .out1(decoder_3_out0[1]), .out2(decoder_3_out0[2]), .out3(decoder_3_out0[3]),
    .out4(decoder_3_out0[4]), .out5(decoder_3_out5[0]), .out6(decoder_3_out5[1]), .out7(decoder_3_out5[2]),
    .sel(out_15[2:0]));
  Decoder #(.enable("false"), .select(2)) decoder_4 (
    .out0(decoder_4_out0), .out1(decoder_4_out1), .out2(decoder_4_out2), .sel(out_13[4:3]));  // open: out3
  D_Flip_Flop BEN (.D(or_9_out), .clk(out_13[35]), .Q(out_47));  // open: Qn, preset, reset
  or or_9 (or_9_out, and_18_out, and_19_out, and_20_out);
  assign controlled_buffer_6_out = decoder_3_out0[0] ? R0_q : 16'bz;  // Controlled_Buffer controlled_buffer_6
  assign controlled_buffer_6_out = decoder_3_out0[1] ? R1_q : 16'bz;  // Controlled_Buffer controlled_buffer_7
  assign controlled_buffer_6_out = decoder_3_out0[2] ? R2_q : 16'bz;  // Controlled_Buffer controlled_buffer_8
  assign controlled_buffer_6_out = decoder_3_out0[3] ? R3_q : 16'bz;  // Controlled_Buffer controlled_buffer_9
  assign controlled_buffer_6_out = decoder_3_out0[4] ? R4_q : 16'bz;  // Controlled_Buffer controlled_buffer_10
  assign controlled_buffer_6_out = decoder_3_out5[0] ? R5_q : 16'bz;  // Controlled_Buffer controlled_buffer_11
  assign controlled_buffer_6_out = decoder_3_out5[1] ? R6_q : 16'bz;  // Controlled_Buffer controlled_buffer_12
  assign controlled_buffer_6_out = decoder_3_out5[2] ? R7_q : 16'bz;  // Controlled_Buffer controlled_buffer_13
  assign bit_extender_5_out = {{11{out_15[4]}}, out_15[4:0]};  // Bit_Extender bit_extender_5
  Multiplexer #(.width(16)) multiplexer_16 (
    .in0(controlled_buffer_6_out), .in1(bit_extender_5_out), .out(multiplexer_16_out), .sel(out_15[5]));
  // Probe on multiplexer_16_out
  not not_7 (not_7_out, in_1);
  or or_10 (or_10_out, in_1, out_13[30]);
  assign controlled_buffer_14_out = decoder_5_out0[0] ? R0_q : 16'bz;  // Controlled_Buffer controlled_buffer_14
  assign controlled_buffer_14_out = decoder_5_out0[1] ? R1_q : 16'bz;  // Controlled_Buffer controlled_buffer_15
  assign controlled_buffer_14_out = decoder_5_out0[2] ? R2_q : 16'bz;  // Controlled_Buffer controlled_buffer_16
  assign controlled_buffer_14_out = decoder_5_out0[3] ? R3_q : 16'bz;  // Controlled_Buffer controlled_buffer_17
  assign controlled_buffer_14_out = decoder_5_out0[4] ? R4_q : 16'bz;  // Controlled_Buffer controlled_buffer_18
  assign controlled_buffer_14_out = decoder_5_out0[5] ? R5_q : 16'bz;  // Controlled_Buffer controlled_buffer_19
  assign controlled_buffer_14_out = decoder_5_out0[6] ? R6_q : 16'bz;  // Controlled_Buffer controlled_buffer_20
  assign controlled_buffer_14_out = decoder_5_out0[7] ? R7_q : 16'bz;  // Controlled_Buffer controlled_buffer_21
  // Probe on controlled_buffer_14_out
  Register #(.width(16)) SSP (.D(multiplexer_17_out), .en(or_10_out), .clk(clock_16_out), .Q(SSP_q));  // open: clr
  Multiplexer #(.width(16)) multiplexer_17 (
    .in0(in_6), .in1(controlled_buffer_14_out), .out(multiplexer_17_out), .sel(not_7_out));
  Register #(.width(16)) USP (.D(controlled_buffer_14_out), .en(out_13[29]), .clk(clock_16_out), .Q(USP_q), .clr(in_1));
  Clock clock_16 (.out(clock_16_out));
  Multiplexer #(.select(2), .width(8)) multiplexer_18 (
    .in0(in_5), .in1({8{1'b0}}), .in2(8'h1), .out(multiplexer_18_out), .sel(out_13[7:6]));  // open: in3
  Decoder #(.enable("false"), .select(3)) decoder_5 (
    .out0(decoder_5_out0[0]), .out1(decoder_5_out0[1]), .out2(decoder_5_out0[2]), .out3(decoder_5_out0[3]),
    .out4(decoder_5_out0[4]), .out5(decoder_5_out0[5]), .out6(decoder_5_out0[6]), .out7(decoder_5_out0[7]),
    .sel(out_56));
  Multiplexer #(.select(2), .width(3)) multiplexer_19 (
    .in0(out_15[11:9]), .in1(out_15[8:6]), .in2(3'b110), .out(out_56), .sel(out_13[15:14]));  // open: in3
  assign controlled_buffer_22_out = decoder_4_out0 ? adder_4_out : 16'bz;  // Controlled_Buffer controlled_buffer_22
  Adder #(.width(16)) adder_4 (
    .a(controlled_buffer_14_out), .b(multiplexer_16_out), .out(adder_4_out));  // open: cin, cout
  assign and_21_out = controlled_buffer_14_out & multiplexer_16_out;  // AND_Gate and_21, 16 bits wide
  assign controlled_buffer_22_out = decoder_4_out1 ? and_21_out : 16'bz;  // Controlled_Buffer controlled_buffer_23
  assign not_8_out = ~controlled_buffer_14_out;  // NOT_Gate not_8, 16 bits wide
  assign controlled_buffer_22_out = decoder_4_out2 ? not_8_out : 16'bz;  // Controlled_Buffer controlled_buffer_24
  Register Vector (.D(multiplexer_18_out), .en(out_13[28]), .clk(clock_17_out), .Q(Vector_q), .clr(in_1));
  Clock clock_17 (.out(clock_17_out));
  // Probe on controlled_buffer_22_out
  Adder #(.width(16)) adder_5 (.a(16'h1), .b(controlled_buffer_14_out), .out(adder_5_out));  // open: cin, cout
  Multiplexer #(.select(2), .width(16)) multiplexer_20 (
    .in0(adder_5_out), .in1(adder_6_out), .in2(SSP_q), .in3(USP_q), .out(multiplexer_20_out),
    .sel(out_13[10:9]));
  Adder #(.width(16)) adder_6 (.a(controlled_buffer_14_out), .b({16{1'b1}}), .out(adder_6_out));  // open: cin, cout
  assign out_16 = out_13[23] ? {8'h1, Vector_q} : 16'bz;  // Controlled_Buffer controlled_buffer_25
  assign out_16 = out_13[25] ? controlled_buffer_22_out : 16'bz;  // Controlled_Buffer controlled_buffer_26
  assign out_16 = out_13[20] ? multiplexer_20_out : 16'bz;  // Controlled_Buffer controlled_buffer_27
  Register #(.width(6)) register_1 (
    .D(multiplexer_21_out), .en(1'b1), .clk(clock_18_out), .Q(register_1_q));  // open: clr
  Clock clock_18 (.out(clock_18_out));
  ROM #(.addrWidth(6), .dataWidth(64)) ControlStore (.addr(register_1_q), .data(ControlStore_data));
  and and_22 (and_22_out, out_13[47], ~out_13[46], out_13[45], out_39);  // AND_Gate
  or or_11 (or_15_out[4], out_13[43], and_22_out);
  and and_23 (and_23_out, out_13[47], ~out_13[46], ~out_13[45], out_8);  // AND_Gate
  or or_12 (or_15_out[3], out_13[42], and_23_out);
  Multiplexer #(.width(6)) multiplexer_21 (
    .in0({out_13[44], or_15_out}), .in1({2'b00, out_15[15:12]}), .out(multiplexer_21_out), .sel(out_13[48]));
  and and_24 (and_24_out, ~out_13[47], out_13[46], ~out_13[45], out_47);  // AND_Gate
  or or_13 (or_15_out[2], out_13[41], and_24_out);
  not not_9 (not_9_out, in_1);
  and and_25 (and_25_out, ~out_13[47], ~out_13[46], out_13[45], out_43);  // AND_Gate
  or or_14 (or_15_out[1], out_13[40], and_25_out);
  or or_15 (or_15_out[0], out_13[39], and_26_out);
  Register #(.trigger("falling"), .width(6)) State (
    .D(multiplexer_21_out), .en(1'b1), .clk(clock_19_out), .Q(_2), .clr(in_1));
  Register #(.trigger("falling"), .width(49)) register_2 (
    .D(controlled_buffer_28_out), .en(1'b1), .clk(clock_19_out), .Q(out_13), .clr(in_1));
  assign controlled_buffer_28_out = not_9_out ? ControlStore_data[48:0] : 49'bz;  // Controlled_Buffer controlled_buffer_28
  Clock clock_19 (.out(clock_19_out));
  and and_26 (and_26_out, ~out_13[47], out_13[46], out_13[45], out_15[11]);  // AND_Gate

  assign _16 = _2;
  assign out_17 = out_13[48];
  assign out_18 = out_13[38];
  assign out_19 = out_13[27];
  assign out_20 = out_13[19:18];
  assign out_21 = out_13[2];
  assign out_22 = out_13[47:45];
  assign out_23 = out_13[37];
  assign out_24 = out_13[26];
  assign out_25 = out_13[17:16];
  assign out_26 = out_13[1];
  assign out_27 = out_13[44:39];
  assign out_28 = out_13[36];
  assign out_29 = out_13[25];
  assign out_30 = out_13[15:14];
  assign out_31 = out_13[0];
  assign out_32 = out_13[35];
  assign out_33 = out_13[24];
  assign out_34 = out_13[13];
  assign out_35 = out_8;
  assign out_36 = out_13[34];
  assign out_37 = out_13[23];
  assign out_38 = out_13[12:11];
  assign out_40 = out_13[33];
  assign out_41 = out_13[22];
  assign out_42 = out_13[10:9];
  assign out_44 = out_13[32];
  assign out_45 = out_13[21];
  assign out_46 = out_13[8];
  assign out_48 = out_13[31];
  assign out_49 = out_13[20];
  assign out_50 = out_13[7:6];
  assign out_51 = out_13[30];
  assign out_52 = out_13[5];
  assign out_54 = out_13[29];
  assign out_55 = out_13[4:3];
  assign out_57 = out_13[28];

  // Other names for the same wires on the sheet: DataBus[15:0] = out_16; CC[2:0] = out_14; Priority[2:0] = out_11;
  //   Priv = out_8; PSR15 = out_8; Instruction[15:0] = out_15; IR15_12[3:0] = out_15[15:12]; BEN = out_47;
  //   DR[2:0] = out_53; iCC[2:0] = in_4; IR2_0[2:0] = out_15[2:0]; IR5 = out_15[5]; IR8_6[2:0] = out_15[8:6];
  //   IR11_9[2:0] = out_15[11:9]; IR11 = out_15[11]; INT = out_39; INTP[2:0] = Interrupts; INTV[7:0] = in_5;
  //   iSSP[15:0] = in_6; Microinstruction[48:0] = out_13; Set_Priv = out_13[0]; R_W = out_13[1]; MIO_EN = out_13[2];
  //   ALUK[1:0] = out_13[4:3]; PSRMUX = out_13[5]; VectorMUX[1:0] = out_13[7:6]; MARMUX = out_13[8];
  //   SPMUX[1:0] = out_13[10:9]; ADDR2MUX[1:0] = out_13[12:11]; ADDR1MUX = out_13[13]; SR1MUX[1:0] = out_13[15:14];
  //   DRMUX[1:0] = out_13[17:16]; PCMUX[1:0] = out_13[19:18]; GateSP = out_13[20]; GatePSR = out_13[21];
  //   GatePCm1 = out_13[22]; GateVector = out_13[23]; GateMARMUX = out_13[24]; GateALU = out_13[25];
  //   GateMDR = out_13[26]; GatePC = out_13[27]; LD_Vector = out_13[28]; LD_SavedUSP = out_13[29];
  //   LD_SavedSSP = out_13[30]; LD_Priv = out_13[31]; LD_PC = out_13[32]; LD_CC = out_13[33]; LD_REG = out_13[34];
  //   LD_BEN = out_13[35]; LD_IR = out_13[36]; LD_MDR = out_13[37]; LD_MAR = out_13[38]; J[5:0] = out_13[44:39];
  //   COND[2:0] = out_13[47:45]; IRD = out_13[48]; orig[15:0] = Reset_Values; PC[15:0] = out_12; PCm1[15:0] = out_9;
  //   R = out_43; ResetSim = in_1; SR1[2:0] = out_56; State[5:0] = _2

  // Notes on the sheet:
  //   Reset_Values: initial=0x3000
  //   in_4: initial=0x2
  //   in_6: initial=0x3000
  //   in_1: initial=0x1
  //   Console +
  //    Keyboard
  //   Mem Mapping
  //   To Run:
  //   1. Ensure `ResetSim` is enabled, then toggle the clock on and off.
  //   2. Load a program .bin into main memory using "Load Image"
  //   3. Disable `Reset Sim` and start toggling the clock!
  //   (You can also enable "Auto-Tick" under the "Simulate Menu") 
  //   To Reset: Perform steps 1&3 above
  //   TODOs:
  //   How to handle HALT?
  //   Set keyboard interrupt: KBSR |= 2^14
  //   Control Signals
  //   Data Path (Fig C.8)
  //   I/O Registers
  //   + Logic
  //   DR
  //   (Fig. C.6)
  //   Reg File
  //   SR2
  //   Interrupts
  //   SR1
  //   contents of ControlStore (hex, n*v repeats v):
  //   490000000000 90602004000 cc001001100 bc001001100 6a0000000000 90602004008 cc001006900 bc001006900
  //   92400100a100 90602004010 c4001001100 ec001001100 90101086000 92a090200080 90601001100 9aa080200000
  //   280000000006 0 b0c108000000 0 90508092000 90508093800 90100081100 82001002100 2c2000000004
  //   2ca000000004 cc004000000 90604000000 2e2408010004 2ea000000004 90104040000 bc004000000 1000800000000
  //   30a000000004 998400128000 101004000000 322000000004 14c400128200 138104040000 144400128000
  //   342000000004 348000000006 110284000020 17a000400000 182090200040 128420128400 0 184400128200
  //   380000000006 92a090a00000 1a4000800000 90000000000 3a2000000004 1c4400128200 90104040000 0
  //   3c0000000006 1e4400128200 1ca008000000 90440128600 3e0000000006 1a8420128400 1a4001000000
  //   Microsequencer (Fig. C.5)
endmodule
